// Logisim project ALU.circ as structural Verilog: 1 circuit, main circuit main
module main (
  input  in_1,
  input  [7:0] A,
  input  [7:0] B,
  input  [3:0] Instruction,
  output GZ,
  output EQ,
  output LZ,
  output GE,
  output LE
);

  wire [7:0] multiplier_1_out, n8_bit_adder_1_out_4, n8_bit_subtractor_1_out_3;

  _8_bit_Adder u_8_bit_adder_1 (
    .out_4(n8_bit_adder_1_out_4), .in_1(in_1), .Input__One_of_the_inputs_to_be_added(A),
    .Input__One_of_the_inputs_to_be_added_2(B));  // open: Carry_Out
  _8_bit_Subtractor u_8_bit_subtractor_1 (.in_1(A), .in_2(B), .out_3(n8_bit_subtractor_1_out_3));  // open: out_4
  // _8_bit_circuit 8_bit_circuit_1: pin names not known; wires that end beside it: 1'b0, 1'b1, 1'b0, A, {8{1'b0}}, LZ, EQ, GZ
  or or_1 (GE, GZ, EQ);
  Multiplier multiplier_1 (.out(multiplier_1_out));  // open: a, b, cin, cout
  or or_2 (LE, EQ, LZ);
  Multiplexer #(.select(4), .width(8), .enable("false")) multiplexer_1 (
    .in0({8{1'b0}}), .in1({8{1'b0}}), .in2({8{1'b0}}), .in3({8{1'b0}}), .in4(n8_bit_adder_1_out_4),
    .in5(n8_bit_subtractor_1_out_3), .in6({8{1'b0}}), .in7(multiplier_1_out), .in8({8{1'b0}}),
    .in9({8{1'b0}}), .in10({8{1'b0}}), .in11({8{1'b0}}), .in12({8{1'b0}}), .in13({8{1'b0}}),
    .in14({8{1'b0}}), .in15({8{1'b0}}), .sel(Instruction));  // open: out
endmodule
