// Logisim project fetch.circ as structural Verilog: 1 circuit, main circuit main
// 32
module main (
);

  wire [3:0] bitselector_2_out, bitselector_3_out, bitselector_4_out;
  wire [15:0] adder_1_out, bitselector_1_out, undriven;
  wire [31:0] rom_1_data;

  ROM #(.addrWidth(16), .dataWidth(32)) rom_1 (.addr(undriven), .data(rom_1_data));  // open: sel
  BitSelector #(.width(32), .group(16)) bitselector_1 (.in(rom_1_data), .out(bitselector_1_out), .sel(1'b1));
  BitSelector #(.width(32), .group(4)) bitselector_2 (.in(rom_1_data), .out(bitselector_2_out), .sel(3'b011));
  BitSelector #(.width(32), .group(4)) bitselector_3 (.in(rom_1_data), .out(bitselector_3_out), .sel(3'b010));
  BitSelector #(.width(32), .group(4)) bitselector_4 (.in(rom_1_data), .out(bitselector_4_out), .sel(3'b001));
  Adder #(.width(16)) adder_1 (.b(undriven), .out(adder_1_out), .cin(1'b1));  // open: a, cout

  // Notes on the sheet:
  //   PC_IN
  //   CONST / NEW_PC
  //   R_B
  //   R_A / FLAG
  //   OP_CODE
  //   PC_OUT
endmodule
