// Logisim project final.circ as structural Verilog: 5 circuits, main circuit main
// %ecx
module main (
  output [3:0] Instruction_Code,
  output [7:0] Output_Debug,
  output [2:0] Register_A,
  output [7:0] out_4,
  output [2:0] Register_B,
  output [7:0] Memory_Address_A,
  output [7:0] Memory_Address_B,
  output EQ,
  output LE,
  output GE,
  output LZ,
  output GZ
);

  wire decoder_1_out0, decoder_1_out1, decoder_1_out2, decoder_1_out3, decoder_1_out4, decoder_1_out5,
       decoder_1_out6, decoder_1_out7, decoder_1_out8, fetch_1_enable, or_1_out, or_2_out, or_3_out;
  wire [2:0] multiplexer_2_out;
  wire [3:0] fetch_1_ra___flag, fetch_1_rb;
  wire [7:0] alu_1_output, fetch_1_op_code, fetch_1_pc_out, memory_bus_1_read_data, multiplexer_1_out,
       multiplexer_3_out, multiplexer_4_out, multiplexer_5_out;

  fetch fetch_1 (
    .PC_IN(multiplexer_1_out), .OP_CODE(fetch_1_op_code), .RA___FLAG(fetch_1_ra___flag), .RB(fetch_1_rb),
    .CONST___NEW_PC(out_4), .ENABLE(fetch_1_enable), .PC_OUT(fetch_1_pc_out), .HALT(decoder_1_out8));
  Multiplexer #(.width(8), .enable("false")) multiplexer_1 (
    .in0(fetch_1_pc_out), .in1(out_4), .out(multiplexer_1_out), .sel(decoder_1_out7));
  BitSelector #(.group(4)) bitselector_1 (.in(fetch_1_op_code), .out(Instruction_Code), .sel(1'b0));
  BitSelector #(.width(4), .group(3)) bitselector_2 (.in(fetch_1_ra___flag), .out(Register_A), .sel(1'b0));
  BitSelector #(.width(4), .group(3)) bitselector_3 (.in(fetch_1_rb), .out(Register_B), .sel(1'b0));
  Decoder #(.select(4)) decoder_1 (
    .out0(decoder_1_out0), .out1(decoder_1_out1), .out2(decoder_1_out2), .out3(decoder_1_out3),
    .out4(decoder_1_out4), .out5(decoder_1_out5), .out6(decoder_1_out6), .out7(decoder_1_out7),
    .out8(decoder_1_out8), .sel(Instruction_Code), .en(fetch_1_enable));  // open: out9, out10, out11, out12, out13, out14, out15
  Multiplexer #(.width(3), .enable("false")) multiplexer_2 (
    .in0(Register_B), .in1(Register_A), .out(multiplexer_2_out), .sel(decoder_1_out3));
  or or_1 (or_1_out, decoder_1_out1, decoder_1_out2, decoder_1_out3, decoder_1_out4, decoder_1_out5, decoder_1_out6);
  Multiplexer #(.width(8), .enable("false")) multiplexer_3 (
    .in0(Memory_Address_A), .in1(Memory_Address_B), .out(multiplexer_3_out), .sel(decoder_1_out0));
  Multiplexer #(.width(8), .enable("false")) multiplexer_4 (
    .in0(memory_bus_1_read_data), .in1(Memory_Address_A), .out(multiplexer_4_out), .sel(decoder_1_out2));
  or or_2 (or_2_out, decoder_1_out4, decoder_1_out5, decoder_1_out6);
  Multiplexer #(.width(8), .enable("false")) multiplexer_5 (
    .in0(multiplexer_4_out), .in1(alu_1_output), .out(multiplexer_5_out), .sel(or_2_out));
  Multiplexer #(.width(8), .enable("false")) multiplexer_6 (
    .in0(multiplexer_5_out), .in1(out_4), .out(Output_Debug), .sel(decoder_1_out3));
  _8x32_RF u_8x32_rf_1 (
    .Write1(Output_Debug), .Register_1_2(multiplexer_2_out), .WE(or_1_out), .Read1(Memory_Address_A),
    .RE(or_3_out), .Register_1(Register_A), .Read2(Memory_Address_B), .Register_2(Register_B));  // open: Register_2_2, Write2
  memory_bus memory_bus_1 (
    .Address(multiplexer_3_out), .WE(decoder_1_out0), .RE(decoder_1_out1), .Write_Data(Memory_Address_A),
    .Read_Data(memory_bus_1_read_data));
  or or_3 (or_3_out, decoder_1_out4, decoder_1_out2, decoder_1_out1, decoder_1_out0, decoder_1_out5);
  ALU alu_1 (
    .A(Memory_Address_B), .B(Memory_Address_A), .LZ(LZ), .LE(LE), .EQ(EQ), .GE(GE), .GZ(GZ),
    .Instruction(Instruction_Code), .Output(alu_1_output), .in_3(fetch_1_enable));
endmodule

module _8x32_RF (
  input  [7:0] Write1,
  input  RE,
  input  [2:0] Register_1,
  input  [2:0] Register_1_2,
  input  WE,
  input  [2:0] Register_2,
  input  [2:0] Register_2_2,
  input  [7:0] Write2,
  output [7:0] Read1,
  output [7:0] Read2
);

  wire clock_1_out, decoder_1_out0, decoder_1_out1, decoder_1_out2, decoder_1_out3, decoder_1_out4,
       decoder_1_out5, decoder_1_out6, decoder_1_out7, decoder_2_out0, decoder_2_out1, decoder_2_out2,
       decoder_2_out3, decoder_2_out4, decoder_2_out5, decoder_2_out6, decoder_2_out7, decoder_3_out0,
       decoder_3_out1, decoder_3_out2, decoder_3_out3, decoder_3_out4, decoder_3_out5, decoder_3_out6,
       decoder_3_out7, decoder_4_out0, decoder_4_out1, decoder_4_out2, decoder_4_out3, decoder_4_out4,
       decoder_4_out5, decoder_4_out6, decoder_4_out7, or_1_out, or_2_out, or_3_out, or_4_out, or_5_out,
       or_6_out, or_7_out, or_8_out;
  wire [7:0] eax_q, ebp_q, ebx_q, ecx_q, edi_q, edx_q, esi_q, esp_q, multiplexer_1_out, multiplexer_2_out,
       multiplexer_3_out, multiplexer_4_out, multiplexer_5_out, multiplexer_6_out, multiplexer_7_out,
       multiplexer_8_out;

  Decoder #(.select(3)) decoder_1 (
    .out0(decoder_1_out0), .out1(decoder_1_out1), .out2(decoder_1_out2), .out3(decoder_1_out3),
    .out4(decoder_1_out4), .out5(decoder_1_out5), .out6(decoder_1_out6), .out7(decoder_1_out7),
    .sel(Register_1_2), .en(WE));
  Decoder #(.select(3)) decoder_2 (
    .out0(decoder_2_out0), .out1(decoder_2_out1), .out2(decoder_2_out2), .out3(decoder_2_out3),
    .out4(decoder_2_out4), .out5(decoder_2_out5), .out6(decoder_2_out6), .out7(decoder_2_out7),
    .sel(Register_2_2), .en(WE));
  Multiplexer #(.width(8)) multiplexer_1 (
    .in0(Write2), .in1(Write1), .out(multiplexer_1_out), .sel(decoder_1_out0));  // open: en
  Multiplexer #(.width(8)) multiplexer_2 (
    .in0(Write2), .in1(Write1), .out(multiplexer_2_out), .sel(decoder_1_out1));  // open: en
  Multiplexer #(.width(8)) multiplexer_3 (
    .in0(Write2), .in1(Write1), .out(multiplexer_3_out), .sel(decoder_1_out2));  // open: en
  Multiplexer #(.width(8)) multiplexer_4 (
    .in0(Write2), .in1(Write1), .out(multiplexer_4_out), .sel(decoder_1_out3));  // open: en
  Multiplexer #(.width(8)) multiplexer_5 (
    .in0(Write2), .in1(Write1), .out(multiplexer_5_out), .sel(decoder_1_out4));  // open: en
  Multiplexer #(.width(8)) multiplexer_6 (
    .in0(Write2), .in1(Write1), .out(multiplexer_6_out), .sel(decoder_1_out5));  // open: en
  Multiplexer #(.width(8)) multiplexer_7 (
    .in0(Write2), .in1(Write1), .out(multiplexer_7_out), .sel(decoder_1_out6));  // open: en
  Multiplexer #(.width(8)) multiplexer_8 (
    .in0(Write2), .in1(Write1), .out(multiplexer_8_out), .sel(decoder_1_out7));  // open: en
  or or_1 (or_1_out, decoder_1_out0, decoder_2_out0);
  or or_2 (or_2_out, decoder_1_out1, decoder_2_out1);
  or or_3 (or_3_out, decoder_1_out2, decoder_2_out2);
  or or_4 (or_4_out, decoder_1_out3, decoder_2_out3);
  or or_5 (or_5_out, decoder_1_out4, decoder_2_out4);
  or or_6 (or_6_out, decoder_1_out5, decoder_2_out5);
  or or_7 (or_7_out, decoder_1_out6, decoder_2_out6);
  or or_8 (or_8_out, decoder_1_out7, decoder_2_out7);
  Clock clock_1 (.out(clock_1_out));
  Register eax (.D(multiplexer_1_out), .en(or_1_out), .Q(eax_q), .clk(clock_1_out));  // open: clr
  Register ecx (.D(multiplexer_2_out), .en(or_2_out), .Q(ecx_q), .clk(clock_1_out));  // open: clr
  Register edx (.D(multiplexer_3_out), .en(or_3_out), .Q(edx_q), .clk(clock_1_out));  // open: clr
  Register ebx (.D(multiplexer_4_out), .en(or_4_out), .Q(ebx_q), .clk(clock_1_out));  // open: clr
  Register esi (.D(multiplexer_5_out), .en(or_5_out), .Q(esi_q), .clk(clock_1_out));  // open: clr
  Register edi (.D(multiplexer_6_out), .en(or_6_out), .Q(edi_q), .clk(clock_1_out));  // open: clr
  Register esp (.D(multiplexer_7_out), .en(or_7_out), .Q(esp_q), .clk(clock_1_out));  // open: clr
  Register ebp (.D(multiplexer_8_out), .en(or_8_out), .Q(ebp_q), .clk(clock_1_out));  // open: clr
  assign Read1 = decoder_3_out0 ? eax_q : 8'bz;  // Controlled_Buffer controlled_buffer_1
  assign Read1 = decoder_3_out1 ? ecx_q : 8'bz;  // Controlled_Buffer controlled_buffer_2
  assign Read1 = decoder_3_out2 ? edx_q : 8'bz;  // Controlled_Buffer controlled_buffer_3
  assign Read1 = decoder_3_out3 ? ebx_q : 8'bz;  // Controlled_Buffer controlled_buffer_4
  assign Read1 = decoder_3_out4 ? esi_q : 8'bz;  // Controlled_Buffer controlled_buffer_5
  assign Read1 = decoder_3_out5 ? edi_q : 8'bz;  // Controlled_Buffer controlled_buffer_6
  assign Read1 = decoder_3_out6 ? esp_q : 8'bz;  // Controlled_Buffer controlled_buffer_7
  assign Read1 = decoder_3_out7 ? ebp_q : 8'bz;  // Controlled_Buffer controlled_buffer_8
  assign Read2 = decoder_4_out0 ? eax_q : 8'bz;  // Controlled_Buffer controlled_buffer_9
  assign Read2 = decoder_4_out1 ? ecx_q : 8'bz;  // Controlled_Buffer controlled_buffer_10
  assign Read2 = decoder_4_out2 ? edx_q : 8'bz;  // Controlled_Buffer controlled_buffer_11
  assign Read2 = decoder_4_out3 ? ebx_q : 8'bz;  // Controlled_Buffer controlled_buffer_12
  assign Read2 = decoder_4_out4 ? esi_q : 8'bz;  // Controlled_Buffer controlled_buffer_13
  assign Read2 = decoder_4_out5 ? edi_q : 8'bz;  // Controlled_Buffer controlled_buffer_14
  assign Read2 = decoder_4_out6 ? esp_q : 8'bz;  // Controlled_Buffer controlled_buffer_15
  assign Read2 = decoder_4_out7 ? ebp_q : 8'bz;  // Controlled_Buffer controlled_buffer_16
  Decoder #(.select(3)) decoder_3 (
    .out0(decoder_3_out0), .out1(decoder_3_out1), .out2(decoder_3_out2), .out3(decoder_3_out3),
    .out4(decoder_3_out4), .out5(decoder_3_out5), .out6(decoder_3_out6), .out7(decoder_3_out7),
    .sel(Register_1), .en(RE));
  Decoder #(.select(3)) decoder_4 (
    .out0(decoder_4_out0), .out1(decoder_4_out1), .out2(decoder_4_out2), .out3(decoder_4_out3),
    .out4(decoder_4_out4), .out5(decoder_4_out5), .out6(decoder_4_out6), .out7(decoder_4_out7),
    .sel(Register_2), .en(RE));
endmodule

module memory_bus (
  input  [7:0] Address,
  input  [7:0] Write_Data,
  input  WE,
  input  RE,
  output [7:0] Read_Data
);

  wire clock_1_out, not_1_out;
  wire [7:0] ram_1_data;

  Clock clock_1 (.out(clock_1_out));
  RAM ram_1 (.addr(Address), .data(ram_1_data), .clk(clock_1_out), .ld(not_1_out));  // open: sel, clr
  not not_1 (not_1_out, WE);
  assign ram_1_data = WE ? Read_Data : 8'bz;  // Controlled_Buffer controlled_buffer_1
  assign Read_Data = RE ? ram_1_data : 8'bz;  // Controlled_Buffer controlled_buffer_2
  assign Read_Data = WE ? Write_Data : 8'bz;  // Controlled_Buffer controlled_buffer_3
endmodule

module fetch (
  input  [7:0] PC_IN,
  input  HALT,
  output [7:0] OP_CODE,
  output [3:0] RA___FLAG,
  output [3:0] RB,
  output [7:0] CONST___NEW_PC,
  output ENABLE,
  output [7:0] PC_OUT
);

  wire clock_1_out, demultiplexer_1_out0, demultiplexer_1_out1;
  wire [1:0] bitselector_1_out;
  wire [7:0] adder_1_out, counter_1_q, multiplexer_1_out, register_1_q, register_3_q, rom_1_data;

  Clock clock_1 (.out(clock_1_out));
  Counter #(.max('h2)) counter_1 (.Q(counter_1_q), .clk(clock_1_out));  // open: load, D, count, carry, clr
  Register register_1 (.D(PC_IN), .Q(register_1_q), .clk(clock_1_out));  // open: en, clr
  BitSelector #(.group(2)) bitselector_1 (.in(counter_1_q), .out(bitselector_1_out), .sel(2'b00));
  Adder adder_1 (.a(counter_1_q), .b(register_1_q), .out(adder_1_out));  // open: cin, cout
  Multiplexer #(.width(8), .enable("false")) multiplexer_1 (
    .in0(adder_1_out), .in1(register_1_q), .out(multiplexer_1_out), .sel(HALT));
  Demultiplexer #(.select(2)) demultiplexer_1 (
    .out0(demultiplexer_1_out0), .out1(demultiplexer_1_out1), .out2(ENABLE), .in(1'b1),
    .sel(bitselector_1_out));  // open: out3, en
  ROM rom_1 (.addr(multiplexer_1_out), .data(rom_1_data));  // open: sel
  Adder adder_2 (.a(8'h3), .b(register_1_q), .out(PC_OUT));  // open: cin, cout
  Register register_2 (.D(rom_1_data), .en(demultiplexer_1_out0), .Q(OP_CODE), .clk(clock_1_out));  // open: clr
  BitSelector #(.group(4)) bitselector_2 (.in(register_3_q), .out(RA___FLAG), .sel(1'b0));
  Register register_3 (.D(rom_1_data), .en(demultiplexer_1_out1), .Q(register_3_q), .clk(clock_1_out));  // open: clr
  BitSelector #(.group(4)) bitselector_3 (.in(register_3_q), .out(RB), .sel(1'b1));
  Register register_4 (.D(rom_1_data), .en(ENABLE), .Q(CONST___NEW_PC), .clk(clock_1_out));  // open: clr

  // Notes on the sheet:
  //   contents of rom_1 (hex, n*v repeats v):
  //   0 0 0 1 2 3
endmodule

module ALU (
  input  [7:0] A,
  input  [7:0] B,
  input  in_3,
  input  [3:0] Instruction,
  output [7:0] Output,
  output GE,
  output GZ,
  output LZ,
  output LE,
  output EQ
);

  wire clock_1_out, comparator_1_eq, comparator_1_gt, comparator_1_lt, or_1_out, or_2_out;
  wire [7:0] adder_1_out, multiplier_1_out, subtractor_1_out;

  Comparator comparator_1 (.a(A), .b({8{1'b0}}), .gt(comparator_1_gt), .eq(comparator_1_eq), .lt(comparator_1_lt));
  or or_1 (or_1_out, comparator_1_lt, comparator_1_eq);
  Register #(.width(1)) register_1 (.D(comparator_1_lt), .Q(LZ), .clk(clock_1_out));  // open: en, clr
  Adder adder_1 (.a(A), .b(B), .out(adder_1_out));  // open: cin, cout
  Subtractor subtractor_1 (.a(A), .b(B), .out(subtractor_1_out));  // open: bin, bout
  Multiplier multiplier_1 (.a(A), .b(B), .out(multiplier_1_out));  // open: cin, cout
  Register #(.width(1)) register_2 (.D(or_1_out), .Q(LE), .clk(clock_1_out));  // open: en, clr
  or or_2 (or_2_out, comparator_1_eq, comparator_1_gt);
  Register #(.width(1)) register_3 (.D(or_2_out), .Q(GE), .clk(clock_1_out));  // open: en, clr
  Register #(.width(1)) register_4 (.D(comparator_1_eq), .Q(EQ), .clk(clock_1_out));  // open: en, clr
  Register #(.width(1)) register_5 (.D(comparator_1_gt), .Q(GZ), .clk(clock_1_out));  // open: en, clr
  Multiplexer #(.select(4), .width(8)) multiplexer_1 (
    .in0({8{1'b0}}), .in1({8{1'b0}}), .in2({8{1'b0}}), .in3({8{1'b0}}), .in4(adder_1_out),
    .in5(subtractor_1_out), .in6({8{1'b0}}), .in7(multiplier_1_out), .in8({8{1'b0}}), .in9({8{1'b0}}),
    .in10({8{1'b0}}), .in11({8{1'b0}}), .in12({8{1'b0}}), .in13({8{1'b0}}), .in14({8{1'b0}}),
    .in15({8{1'b0}}), .out(Output), .sel(Instruction), .en(in_3));
  Clock clock_1 (.out(clock_1_out));
endmodule
